# Fritzing sketch lab03 (saved by Fritzing 0.9.1b)
breadboards: 1

parts:
  R1 = Resistor [tolerance=±5% resistance=220 package=THT]
  BeagleBone1 = BeagleBone Black
  LED1 = LED - 5mm [color="Red (633nm)" package="5 mm [THT]"]
  LED2 = LED - 5mm [color="Red (633nm)" package="5 mm [THT]"]
  R2 = Resistor [tolerance=±5% resistance=220 package=THT]
  S1 = Pushbutton [package="[THT]"]
  R3 = Trimmer Potentiometer [maximum_resistance=10kΩ package=THT]

nets:
  N1: R1.Pin_0, LED1.cathode
  N2: R1.Pin_1, BeagleBone1.no_name_yet#1, R2.Pin_1
  N3: BeagleBone1.no_name_yet#3, S1.Pin_3, S1.Pin_4
  N4: BeagleBone1.no_name_yet#12, LED1.anode
  N5: BeagleBone1.no_name_yet#20, LED2.anode
  N6: BeagleBone1.no_name_yet#32, R3.leg2
  N7: BeagleBone1.no_name_yet#34, R3.leg1
  N8: BeagleBone1.no_name_yet#36, R3.wiper
  N9: BeagleBone1.no_name_yet#42, S1.Pin_1, S1.Pin_2
  N10: LED2.cathode, R2.Pin_0

notes:
  Manoj
  B13208

custom parts:
  BeagleBone Black: BeagleBone Black rev. A5B
