# Fritzing sketch lab04 (saved by Fritzing 0.9.1b)
breadboards: 1

parts:
  R1 = Resistor [tolerance=±5% resistance=220 package=THT]
  BeagleBone1 = BeagleBone Black
  R2 = Resistor [tolerance=±5% resistance=220 package=THT]
  LED1 = 8x8 LED Matrix (green)

nets:
  N1: R1.Pin_0, BeagleBone1.no_name_yet#20, LED1.D
  N2: R1.Pin_1, BeagleBone1.no_name_yet#3, R2.Pin_1, LED1.+
  N3: BeagleBone1.no_name_yet#1, LED1.-
  N4: BeagleBone1.no_name_yet#19, R2.Pin_0, LED1.C

notes:
  Manoj
  B13208

custom parts:
  BeagleBone Black: BeagleBone Black rev. A5B
  8x8 LED Matrix (green): 8x8 LED Matrix with I2C control (green)
