# Fritzing sketch lab05 (saved by Fritzing 0.9.1b)
breadboards: 1

parts:
  BeagleBone1 = BeagleBone Black
  SONAR2 = Maxbotix MaxSonar Ultrasonic Sensor (Hi-Res)
  R1 = Resistor [tolerance=±5% resistance=220 package=THT]
  R2 = Resistor [tolerance=±5% resistance=220 package=THT]

nets:
  N1: BeagleBone1.no_name_yet#1, SONAR2.GND, R2.Pin_0
  N2: BeagleBone1.no_name_yet#3, SONAR2.+5V
  N3: BeagleBone1.no_name_yet#40, R1.Pin_0, R2.Pin_1
  N4: SONAR2.AN, R1.Pin_1

notes:
  Manoj
  B13208

custom parts:
  BeagleBone Black: BeagleBone Black rev. A5B
  Maxbotix MaxSonar Ultrasonic Sensor (Hi-Res): Maxbotix MaxSonar Hi-Resolution Ultrasonic Sensor HRLV-EZ0, HRLV-EZ1, HRLV-EZ2, HRLV-EZ3, HRLV-EZ4
