# Fritzing sketch lab6 (saved by Fritzing 0.9.1b)
breadboards: 1

parts:
  BeagleBone1 = BeagleBone Black
  LED1 = LED - 3mm [color="Red (633nm)" package="3 mm [THT]"]
  Part1 = Thumb Joystick
  R1 = Resistor [tolerance=±5% resistance=220 package=THT]

nets:
  N1: BeagleBone1.no_name_yet#1, Part1.GND, R1.Pin_0
  N2: BeagleBone1.no_name_yet#3, Part1.VCC
  N3: BeagleBone1.no_name_yet#14, LED1.anode
  N4: BeagleBone1.no_name_yet#15, Part1.SEL
  N5: BeagleBone1.no_name_yet#36, Part1.HORZ
  N6: BeagleBone1.no_name_yet#38, Part1.VERT
  N7: LED1.cathode, R1.Pin_1

notes:
  Manoj
  B13208

custom parts:
  BeagleBone Black: BeagleBone Black rev. A5B
